// Logisim project Single_Cycle_CPU.circ as structural Verilog: 1 circuit, main circuit main
module main (
);

  wire ALUSrc, and_1_out, and_2_out, BneOrBeq, Branch, Clk, clock_1_out, Equal, ExpSrc0, ExpSrc1, ExpSrc2,
       ExRegWrite, Halt, HasExp, IsCOP0, isJAL, isJR, IsRet, IsShamt, IsSyscall, Jump, MemRead, MemtoReg,
       MemWrite, multiplexer_4_out, multiplexer_11_out, not_2_out, not_3_out, not_4_out, not_5_out, or_1_out,
       RegDst, RegRs, RegRt, RegWrite, undriven_2, xor_1_out, ZeroExtend;
  wire [1:0] undriven_3;
  wire [3:0] ALUOp, syscall_decoder_1_hex_2, syscall_decoder_1_hex_3, syscall_decoder_1_hex_4,
       syscall_decoder_1_hex_5;
  wire [4:0] multiplexer_6_out, multiplexer_7_out, multiplexer_9_out, multiplexer_10_out;
  wire [5:0] instruction_statistics_1_p6, instruction_statistics_1_p7;
  wire [15:0] syscall_decoder_1_hex;
  wire [25:0] undriven_4;
  wire [31:0] adder_2_out, adder_3_out, bit_extender_1_out, multiplexer_1_out, multiplexer_3_out,
       multiplexer_5_out, multiplexer_8_out, multiplexer_12_out, multiplexer_13_out, multiplexer_14_out,
       multiplexer_15_out, multiplexer_16_out, multiplexer_17_out, multiplexer_18_out, ram_1_dout,
       regfile_1_p4, regfile_1_p5, register_1_q, register_2_q, register_3_q, register_4_q, register_6_q,
       shifter_1_out, undriven, undriven_5, undriven_6, undriven_7, undriven_8;
  wire [31:4] adder_1_out_2;
  wire [31:28] adder_1_out;

  Register #(.width(32)) register_1 (.Q(register_1_q), .clk(Clk));  // open: D, en, clr
  // Probe on register_1_q
  Adder #(.width(32)) adder_1 (.out({adder_1_out_2, adder_1_out}));  // open: a, b, cin, cout
  Register #(.width(32)) register_2 (.Q(register_2_q));  // open: D, en, clk, clr
  // Probe on register_2_q
  // Probe on register_3_q
  Multiplexer #(.width(32)) multiplexer_1 (
    .in0(multiplexer_18_out), .in1(undriven), .out(multiplexer_1_out), .sel(and_1_out));
  and and_1 (and_1_out, IsRet, IsCOP0);
  Multiplexer multiplexer_2 (.in0(clock_1_out), .in1(1'b0), .out(Clk), .sel(Halt));
  Clock clock_1 (.out(clock_1_out));
  Register #(.width(32)) register_3 (.Q(register_3_q));  // open: D, en, clk, clr
  // Probe on register_4_q
  Multiplexer #(.width(32)) multiplexer_3 (
    .in0({32{1'b0}}), .in1(multiplexer_1_out), .out(multiplexer_3_out), .sel(HasExp));
  not not_1 (HasExp, undriven_2);
  or or_1 (or_1_out, undriven_2, and_1_out);
  Register #(.width(32)) register_4 (.Q(register_4_q));  // open: D, en, clk, clr
  Register #(.width(32)) register_5 (.D(multiplexer_3_out), .clk(multiplexer_4_out));  // open: en, Q, clr
  Multiplexer multiplexer_4 (.in0(Clk), .in1(not_2_out), .out(multiplexer_4_out), .sel(or_1_out));
  not not_2 (not_2_out, Clk);
  // Instruction_Statistics instruction_statistics_1: pin names not known; wires that end beside it: instruction_statistics_1_p6[5], instruction_statistics_1_p6[4], instruction_statistics_1_p6[3], instruction_statistics_1_p6[2], instruction_statistics_1_p6[1], instruction_statistics_1_p6[0], instruction_statistics_1_p7
  Adder #(.width(32)) adder_2 (.b({32{1'b0}}), .out(adder_2_out));  // open: a, cin, cout
  Register #(.width(32)) register_6 (.Q(register_6_q), .clk(HasExp));  // open: D, en, clr
  // CP0 cp0_1: pin names not known; wires that end beside it: Clk, HasExp, ExRegWrite
  control_unit control_unit_1 (
    .op(instruction_statistics_1_p6), .Funct(instruction_statistics_1_p7), .ALUOp(ALUOp), .isJAL(isJAL),
    .isShamt(IsShamt), .MemtoReg(MemtoReg), .RegWrite(RegWrite), .BneOrBeq(BneOrBeq), .ALUSrc(ALUSrc),
    .IsSyscall(IsSyscall), .ZeroExtend(ZeroExtend), .IsCOP0(IsCOP0), .ReadRs(RegRs), .ReadRt(RegRt),
    .MemRead(MemRead), .Jump(Jump), .Branch(Branch), .MemWrite(MemWrite), .RegDst(RegDst), .IsJR(isJR));
  Multiplexer #(.width(32)) multiplexer_5 (
    .in0(undriven_5), .in1(multiplexer_8_out), .out(multiplexer_5_out), .sel(not_3_out));
  Multiplexer #(.width(5)) multiplexer_6 (.out(multiplexer_6_out), .sel(RegDst));  // open: in0, in1
  not not_3 (not_3_out, IsCOP0);
  not not_4 (not_4_out, isJAL);
  Multiplexer #(.width(5)) multiplexer_7 (
    .in0(multiplexer_6_out), .in1({5{1'b0}}), .out(multiplexer_7_out), .sel(isJAL));
  Multiplexer #(.width(32)) multiplexer_8 (
    .in0(adder_2_out), .in1(multiplexer_16_out), .out(multiplexer_8_out), .sel(not_4_out));
  Multiplexer #(.width(5)) multiplexer_9 (.out(multiplexer_9_out));  // open: in0, in1, sel
  Multiplexer #(.width(5)) multiplexer_10 (.out(multiplexer_10_out));  // open: in0, in1, sel
  Multiplexer multiplexer_11 (.in0(RegWrite), .in1(ExRegWrite), .out(multiplexer_11_out), .sel(IsCOP0));
  // regfile regfile_1: pin names not known; wires that end beside it: multiplexer_9_out, multiplexer_7_out, multiplexer_5_out, regfile_1_p4, regfile_1_p5
  Multiplexer #(.width(32)) multiplexer_12 (
    .in0(regfile_1_p5), .in1(undriven_6), .out(multiplexer_12_out), .sel(ALUSrc));
  Bit_Extender #(.in_width(5), .out_width(32), .\type ("zero")) bit_extender_1 (.out(bit_extender_1_out));  // open: in
  Multiplexer #(.width(32)) multiplexer_13 (
    .in0(regfile_1_p4), .in1(undriven_8), .out(multiplexer_13_out), .sel(IsShamt));
  Multiplexer #(.width(32)) multiplexer_14 (
    .in0(multiplexer_12_out), .in1(bit_extender_1_out), .out(multiplexer_14_out), .sel(IsShamt));
  Button button_1 (.out(ExpSrc0));
  syscall_decoder syscall_decoder_1 (
    .clk(Clk), .Enable(IsSyscall), .v0(regfile_1_p4), .a0(undriven_8), .Halt(Halt),
    .Hex({syscall_decoder_1_hex_5, syscall_decoder_1_hex_4, syscall_decoder_1_hex_3, syscall_decoder_1_hex_2, syscall_decoder_1_hex}));
  // alu alu_1: pin names not known; wires that end beside it: multiplexer_14_out
  Button button_2 (.out(ExpSrc1));
  Button button_3 (.out(ExpSrc2));
  RAM #(.dataWidth(32)) ram_1 (.addr(undriven_7[7:0]), .din(undriven_8), .dout(ram_1_dout));  // open: we, oe, clk
  Shifter #(.width(32)) shifter_1 (.in(undriven_6), .\dist ({5{1'b0}}), .out(shifter_1_out));
  xor xor_1 (xor_1_out, Equal, BneOrBeq);
  Hex_Digit_Display hex_digit_display_1 (.value(syscall_decoder_1_hex_5));  // open: dp
  Hex_Digit_Display hex_digit_display_2 (.value(syscall_decoder_1_hex_4));  // open: dp
  Adder #(.width(32)) adder_3 (
    .a({adder_1_out_2, adder_1_out}), .b(shifter_1_out), .out(adder_3_out));  // open: cin, cout
  Hex_Digit_Display hex_digit_display_3 (.value(syscall_decoder_1_hex_3));  // open: dp
  Hex_Digit_Display hex_digit_display_4 (.value(syscall_decoder_1_hex_2));  // open: dp
  and and_2 (and_2_out, Branch, xor_1_out);
  Hex_Digit_Display hex_digit_display_5 (.value(syscall_decoder_1_hex[15:12]));  // open: dp
  Hex_Digit_Display hex_digit_display_6 (.value(syscall_decoder_1_hex[11:8]));  // open: dp
  Multiplexer #(.width(32)) multiplexer_15 (
    .in0({adder_1_out_2, adder_1_out}), .in1(adder_3_out), .out(multiplexer_15_out), .sel(and_2_out));
  not not_5 (not_5_out, Jump);
  Hex_Digit_Display hex_digit_display_7 (.value(syscall_decoder_1_hex[7:4]));  // open: dp
  Hex_Digit_Display hex_digit_display_8 (.value(syscall_decoder_1_hex[3:0]));  // open: dp
  Multiplexer #(.width(32)) multiplexer_16 (
    .in0(undriven_7), .in1(ram_1_dout), .out(multiplexer_16_out), .sel(MemtoReg));
  Multiplexer #(.width(32)) multiplexer_17 (
    .in0({adder_1_out, undriven_4, undriven_3}), .in1(multiplexer_15_out), .out(multiplexer_17_out),
    .sel(not_5_out));
  Multiplexer #(.width(32)) multiplexer_18 (
    .in0(multiplexer_17_out), .in1(regfile_1_p4), .out(multiplexer_18_out), .sel(isJR));
  // Pins of 4 and 32 bits meet at {adder_1_out_2, adder_1_out}
  // Pins of 8 and 32 bits meet at undriven_7

  // Notes on the sheet:
  //   Cycles
  //   Total Cycles
  //   R
  //   J
  //   I
  //   PC Buffer
endmodule
